// Logisim project Registros.circ as structural Verilog: 1 circuit, main circuit main
module main (
);

  wire clock_1_out;
  wire [31:0] PC_q;

  Clock clock_1 (.out(clock_1_out));
  // Probe on PC_q
  Register #(.width(32)) PC (.D(32'h101010a), .en(1'b1), .Q(PC_q), .clk(clock_1_out));  // open: clr
  // Probe on clock_1_out
endmodule
