// Logisim project SA03MIPS.circ as structural Verilog: 10 circuits, main circuit TG00MIPS
module TG00MIPS (
);

  wire clock_1_out, stopclk_1_p1, stopclk_1_p3;

  Clock #(.highDuration(4), .lowDuration(4)) clock_1 (.out(clock_1_out));
  // StopClk stopclk_1: pin names not known; wires that end beside it: stopclk_1_p1, clock_1_out, stopclk_1_p3
  MIPS mips_1 (.clk(stopclk_1_p3), .reset(1'b0), .halt(stopclk_1_p1));
endmodule

// clk
module MIPS (
  input  clk,
  input  reset,
  output halt
);

  wire ALUSrc, ALUToReg, Jump, MemWrite, RD, RegWrite;
  wire [2:0] OpALU;
  wire [3:0] control_alu_1_out;
  wire [4:0] multiplexer_2_out;
  wire [15:0] desp;
  wire [25:16] dir;
  wire [31:0] ALU_result, ExSig_desp, MemData, multiplexer_1_out, multiplexer_3_out, multiplexer_4_out, PC_4,
       PC_q, R_rs, R_rt;
  wire [31:26] \INSTRUCCIÓN ;

  Multiplexer #(.width(32)) multiplexer_1 (
    .in0(PC_4), .in1({PC_4[31:28], dir, desp, 2'b00}), .out(multiplexer_1_out), .sel(Jump));  // open: en
  Register #(.width(32)) PC (.D(multiplexer_1_out), .Q(PC_q), .clk(clk));  // open: en, clr
  Adder #(.width(32)) adder_1 (.a(32'h4), .b(PC_q), .out(PC_4));  // open: cin, cout
  assign ExSig_desp = {{16{desp[15]}}, desp};  // Bit_Extender bit_extender_1
  // Probe on {\INSTRUCCIÓN , dir, desp}
  Instruction_memory instruction_memory_1 (.Read_address(PC_q), .Instruction({\INSTRUCCIÓN , dir, desp}));
  Multiplexer #(.width(5)) multiplexer_2 (
    .in0(dir[20:16]), .in1(desp[15:11]), .out(multiplexer_2_out), .sel(RD));  // open: en
  Multiplexer #(.width(32)) multiplexer_3 (
    .in0(MemData), .in1(ALU_result), .out(multiplexer_3_out), .sel(ALUToReg));  // open: en
  Unidad_de_Control unidad_de_control_1 (
    .OPCODE(\INSTRUCCIÓN ), .JUMP(Jump), .HALT(halt), .RegWrite(RegWrite), .MemWrite(MemWrite),
    .MemRead(Jump), .ALUtoReg(ALUToReg), .OPALU(OpALU), .RegDST(RD), .ALUSrc(ALUSrc));
  Register_file register_file_1 (
    .Read_Register_1(dir[25:21]), .Read_Register_2(dir[20:16]), .Write_Register(multiplexer_2_out),
    .Write_Data(multiplexer_3_out), .Read_Data_1(R_rs), .Read_Data_2(R_rt), .clk(clk), .reset(reset),
    .Write(RegWrite));
  Multiplexer #(.width(32)) multiplexer_4 (
    .in0(ExSig_desp), .in1(R_rt), .out(multiplexer_4_out), .sel(ALUSrc));  // open: en
  Control_ALU control_alu_1 (.OpALU(OpALU), .funcion(desp[5:0]), .OUT(control_alu_1_out));
  ALU alu_1 (.A(R_rs), .B(multiplexer_4_out), .Result(ALU_result), .Operation(control_alu_1_out));  // open: Z
  // Probe on control_alu_1_out
  Data_Memory_32 data_memory_32_1 (
    .Address(ALU_result), .Write_Data(R_rt), .Read_Data(MemData), .Write(MemWrite), .clk(clk), .reset(reset),
    .Read(Jump));

  // Other names for the same wires on the sheet: OPCODE[5:0] = \INSTRUCCIÓN ; MemRead = Jump; dir[15:0] = desp;
  //   funcion[5:0] = desp[5:0]; INSTRUCCIÓN[25:0] = {dir, desp}; Salto[31:2] = {PC_4[31:28], dir, desp};
  //   rd_t[4:0] = desp[15:11]; rt[4:0] = dir[20:16]; rs[4:0] = dir[25:21]
endmodule

module Register_file (
  input  clk,
  input  reset,
  input  [4:0] Read_Register_1,
  input  [4:0] Read_Register_2,
  input  [4:0] Write_Register,
  input  [31:0] Write_Data,
  input  Write,
  output [31:0] Read_Data_1,
  output [31:0] Read_Data_2
);

  wire decoder_1_out1, decoder_1_out2, decoder_1_out3, decoder_1_out4, decoder_1_out5, decoder_1_out6,
       decoder_1_out7, decoder_1_out8, decoder_1_out9, decoder_1_out10, decoder_1_out11, decoder_1_out12,
       decoder_1_out13, decoder_1_out14, decoder_1_out15, decoder_1_out16, decoder_1_out17, decoder_1_out18,
       decoder_1_out19, decoder_1_out20, decoder_1_out21, decoder_1_out22, decoder_1_out23, decoder_1_out24,
       decoder_1_out25, decoder_1_out26, decoder_1_out27, decoder_1_out28, decoder_1_out29, decoder_1_out30,
       decoder_1_out31;
  wire [31:0] delayer1x32_1_p2, multiplexer_1_out, multiplexer_2_out, R1_q, R2_q, R3_q, R4_q, R5_q, R6_q,
       R7_q, R8_q, R9_q, R10_q, R11_q, R12_q, R13_q, R14_q, R15_q, R16_q, R17_q, R18_q, R19_q, R20_q, R21_q,
       R22_q, R23_q, R24_q, R25_q, R26_q, R27_q, R28_q, R29_q, R30_q, R31_q;

  Decoder #(.select(5), .disabled(0)) decoder_1 (
    .out1(decoder_1_out1), .out2(decoder_1_out2), .out3(decoder_1_out3), .out4(decoder_1_out4),
    .out5(decoder_1_out5), .out6(decoder_1_out6), .out7(decoder_1_out7), .out8(decoder_1_out8),
    .out9(decoder_1_out9), .out10(decoder_1_out10), .out11(decoder_1_out11), .out12(decoder_1_out12),
    .out13(decoder_1_out13), .out14(decoder_1_out14), .out15(decoder_1_out15), .out16(decoder_1_out16),
    .out17(decoder_1_out17), .out18(decoder_1_out18), .out19(decoder_1_out19), .out20(decoder_1_out20),
    .out21(decoder_1_out21), .out22(decoder_1_out22), .out23(decoder_1_out23), .out24(decoder_1_out24),
    .out25(decoder_1_out25), .out26(decoder_1_out26), .out27(decoder_1_out27), .out28(decoder_1_out28),
    .out29(decoder_1_out29), .out30(decoder_1_out30), .out31(decoder_1_out31), .sel(Write_Register),
    .en(Write));  // open: out0
  // Delayer1x32 delayer1x32_1: pin names not known; wires that end beside it: Write_Data, delayer1x32_1_p2
  Register #(.width(32)) R1 (.D(delayer1x32_1_p2), .en(decoder_1_out1), .Q(R1_q), .clk(clk), .clr(reset));
  Register #(.width(32)) R2 (.D(delayer1x32_1_p2), .en(decoder_1_out2), .Q(R2_q), .clk(clk), .clr(reset));
  Register #(.width(32)) R3 (.D(delayer1x32_1_p2), .en(decoder_1_out3), .Q(R3_q), .clk(clk), .clr(reset));
  Register #(.width(32)) R4 (.D(delayer1x32_1_p2), .en(decoder_1_out4), .Q(R4_q), .clk(clk), .clr(reset));
  Register #(.width(32)) R5 (.D(delayer1x32_1_p2), .en(decoder_1_out5), .Q(R5_q), .clk(clk), .clr(reset));
  Register #(.width(32)) R6 (.D(delayer1x32_1_p2), .en(decoder_1_out6), .Q(R6_q), .clk(clk), .clr(reset));
  Register #(.width(32)) R7 (.D(delayer1x32_1_p2), .en(decoder_1_out7), .Q(R7_q), .clk(clk), .clr(reset));
  Register #(.width(32)) R8 (.D(delayer1x32_1_p2), .en(decoder_1_out8), .Q(R8_q), .clk(clk), .clr(reset));
  Register #(.width(32)) R9 (.D(delayer1x32_1_p2), .en(decoder_1_out9), .Q(R9_q), .clk(clk), .clr(reset));
  Register #(.width(32)) R10 (.D(delayer1x32_1_p2), .en(decoder_1_out10), .Q(R10_q), .clk(clk), .clr(reset));
  Register #(.width(32)) R11 (.D(delayer1x32_1_p2), .en(decoder_1_out11), .Q(R11_q), .clk(clk), .clr(reset));
  Register #(.width(32)) R12 (.D(delayer1x32_1_p2), .en(decoder_1_out12), .Q(R12_q), .clk(clk), .clr(reset));
  Register #(.width(32)) R13 (.D(delayer1x32_1_p2), .en(decoder_1_out13), .Q(R13_q), .clk(clk), .clr(reset));
  Register #(.width(32)) R14 (.D(delayer1x32_1_p2), .en(decoder_1_out14), .Q(R14_q), .clk(clk), .clr(reset));
  Register #(.width(32)) R15 (.D(delayer1x32_1_p2), .en(decoder_1_out15), .Q(R15_q), .clk(clk), .clr(reset));
  Register #(.width(32)) R16 (.D(delayer1x32_1_p2), .en(decoder_1_out16), .Q(R16_q), .clk(clk), .clr(reset));
  Register #(.width(32)) R17 (.D(delayer1x32_1_p2), .en(decoder_1_out17), .Q(R17_q), .clk(clk), .clr(reset));
  Register #(.width(32)) R18 (.D(delayer1x32_1_p2), .en(decoder_1_out18), .Q(R18_q), .clk(clk), .clr(reset));
  Register #(.width(32)) R19 (.D(delayer1x32_1_p2), .en(decoder_1_out19), .Q(R19_q), .clk(clk), .clr(reset));
  Register #(.width(32)) R20 (.D(delayer1x32_1_p2), .en(decoder_1_out20), .Q(R20_q), .clk(clk), .clr(reset));
  Register #(.width(32)) R21 (.D(delayer1x32_1_p2), .en(decoder_1_out21), .Q(R21_q), .clk(clk), .clr(reset));
  Register #(.width(32)) R22 (.D(delayer1x32_1_p2), .en(decoder_1_out22), .Q(R22_q), .clk(clk), .clr(reset));
  Register #(.width(32)) R23 (.D(delayer1x32_1_p2), .en(decoder_1_out23), .Q(R23_q), .clk(clk), .clr(reset));
  Register #(.width(32)) R24 (.D(delayer1x32_1_p2), .en(decoder_1_out24), .Q(R24_q), .clk(clk), .clr(reset));
  Register #(.width(32)) R25 (.D(delayer1x32_1_p2), .en(decoder_1_out25), .Q(R25_q), .clk(clk), .clr(reset));
  Register #(.width(32)) R26 (.D(delayer1x32_1_p2), .en(decoder_1_out26), .Q(R26_q), .clk(clk), .clr(reset));
  Register #(.width(32)) R27 (.D(delayer1x32_1_p2), .en(decoder_1_out27), .Q(R27_q), .clk(clk), .clr(reset));
  Register #(.width(32)) R28 (.D(delayer1x32_1_p2), .en(decoder_1_out28), .Q(R28_q), .clk(clk), .clr(reset));
  Register #(.width(32)) R29 (.D(delayer1x32_1_p2), .en(decoder_1_out29), .Q(R29_q), .clk(clk), .clr(reset));
  Register #(.width(32)) R30 (.D(delayer1x32_1_p2), .en(decoder_1_out30), .Q(R30_q), .clk(clk), .clr(reset));
  Register #(.width(32)) R31 (.D(delayer1x32_1_p2), .en(decoder_1_out31), .Q(R31_q), .clk(clk), .clr(reset));
  Multiplexer #(.select(5), .width(32), .enable("false")) multiplexer_1 (
    .in0({32{1'b0}}), .in1(R1_q), .in2(R2_q), .in3(R3_q), .in4(R4_q), .in5(R5_q), .in6(R6_q), .in7(R7_q),
    .in8(R8_q), .in9(R9_q), .in10(R10_q), .in11(R11_q), .in12(R12_q), .in13(R13_q), .in14(R14_q),
    .in15(R15_q), .in16(R16_q), .in17(R17_q), .in18(R18_q), .in19(R19_q), .in20(R20_q), .in21(R21_q),
    .in22(R22_q), .in23(R23_q), .in24(R24_q), .in25(R25_q), .in26(R26_q), .in27(R27_q), .in28(R28_q),
    .in29(R29_q), .in30(R30_q), .in31(R31_q), .out(multiplexer_1_out), .sel(Read_Register_1));
  Multiplexer #(.select(5), .width(32), .enable("false")) multiplexer_2 (
    .in0({32{1'b0}}), .in1(R1_q), .in2(R2_q), .in3(R3_q), .in4(R4_q), .in5(R5_q), .in6(R6_q), .in7(R7_q),
    .in8(R8_q), .in9(R9_q), .in10(R10_q), .in11(R11_q), .in12(R12_q), .in13(R13_q), .in14(R14_q),
    .in15(R15_q), .in16(R16_q), .in17(R17_q), .in18(R18_q), .in19(R19_q), .in20(R20_q), .in21(R21_q),
    .in22(R22_q), .in23(R23_q), .in24(R24_q), .in25(R25_q), .in26(R26_q), .in27(R27_q), .in28(R28_q),
    .in29(R29_q), .in30(R30_q), .in31(R31_q), .out(multiplexer_2_out), .sel(Read_Register_2));
  // Delayer1x32 delayer1x32_2: pin names not known; wires that end beside it: multiplexer_1_out, Read_Data_1
  // Delayer1x32 delayer1x32_3: pin names not known; wires that end beside it: multiplexer_2_out, Read_Data_2
endmodule

module ALU (
  input  [3:0] Operation,
  input  [31:0] A,
  input  [31:0] B,
  output Z,
  output [31:0] Result
);

  wire nor_1_out;
  wire [0:0] comparator_1_lt;
  wire [31:0] adder_1_out, and_1_out, multiplexer_1_out, multiplexer_2_out, multiplexer_3_out, not_1_out,
       not_2_out, or_1_out;

  assign not_1_out = ~A;  // NOT_Gate not_1, 32 bits wide
  assign not_2_out = ~B;  // NOT_Gate not_2, 32 bits wide
  Comparator #(.width(32)) comparator_1 (.a(A), .b(B), .lt(comparator_1_lt[0]));  // open: gt, eq
  Multiplexer #(.width(32), .enable("false")) multiplexer_1 (
    .in0(A), .in1(not_1_out), .out(multiplexer_1_out), .sel(Operation[3]));
  Multiplexer #(.width(32), .enable("false")) multiplexer_2 (
    .in0(B), .in1(not_2_out), .out(multiplexer_2_out), .sel(Operation[2]));
  assign and_1_out = multiplexer_1_out & multiplexer_2_out;  // AND_Gate and_1, 32 bits wide
  assign or_1_out = multiplexer_1_out | multiplexer_2_out;  // OR_Gate or_1, 32 bits wide
  Adder #(.width(32)) adder_1 (
    .a(multiplexer_1_out), .b(multiplexer_2_out), .out(adder_1_out), .cin(Operation[2]));  // open: cout
  Multiplexer #(.select(2), .width(32), .enable("false")) multiplexer_3 (
    .in0(and_1_out), .in1(or_1_out), .in2(adder_1_out), .in3({{31{1'b0}}, comparator_1_lt[0]}),
    .out(multiplexer_3_out), .sel(Operation[1:0]));
  nor nor_1 (nor_1_out, multiplexer_3_out[0], multiplexer_3_out[1], multiplexer_3_out[2], multiplexer_3_out[3], multiplexer_3_out[4], multiplexer_3_out[5], multiplexer_3_out[6], multiplexer_3_out[7], multiplexer_3_out[8], multiplexer_3_out[9], multiplexer_3_out[10], multiplexer_3_out[11], multiplexer_3_out[12], multiplexer_3_out[13], multiplexer_3_out[14], multiplexer_3_out[15], multiplexer_3_out[16], multiplexer_3_out[17], multiplexer_3_out[18], multiplexer_3_out[19], multiplexer_3_out[20], multiplexer_3_out[21], multiplexer_3_out[22], multiplexer_3_out[23], multiplexer_3_out[24], multiplexer_3_out[25], multiplexer_3_out[26], multiplexer_3_out[27], multiplexer_3_out[28], multiplexer_3_out[29], multiplexer_3_out[30], multiplexer_3_out[31]);
  // Delayer2x32 delayer2x32_1: pin names not known; wires that end beside it: multiplexer_3_out, Result
  // Delayer2x1 delayer2x1_1: pin names not known; wires that end beside it: nor_1_out, Z

  // Notes on the sheet:
  //   0001    OR
  //   Operation    Function
  //   0000    AND
  //   0010    add
  //   0110    subtract
  //   0111    set on less than
  //   1100    NOR
endmodule

module Data_Memory_32 (
  input  Write,
  input  [31:0] Address,
  input  [31:0] Write_Data,
  input  clk,
  input  reset,
  input  Read,
  output [31:0] Read_Data
);

  wire [9:0] bitselector_1_out;
  wire [31:0] delayer2x32_1_p2, ram_1_data;

  BitSelector #(.width(32), .group(10)) bitselector_1 (.in(Address), .out(bitselector_1_out), .sel(2'b00));
  // Delayer2x32 delayer2x32_1: pin names not known; wires that end beside it: Write_Data, delayer2x32_1_p2
  RAM #(.dataWidth(32), .bus("separate"), .Datafile_on_reset("TG00ram.txt")) ram_1 (
    .addr(bitselector_1_out[9:2]), .din(delayer2x32_1_p2), .data(ram_1_data), .str(Write), .sel(1'b1),
    .clk(clk), .ld(Read), .clr(reset));
  // Delayer2x32 delayer2x32_2: pin names not known; wires that end beside it: ram_1_data, Read_Data

  // Notes on the sheet:
  //   Memoria de 32 bits direccionable a nivel de byte
  //   Tan solo implementadas las 256 primeras posiciones de 32 bits o 1024 bytes
endmodule

module Instruction_memory (
  input  [31:0] Read_address,
  output [31:0] Instruction
);

  wire [6:0] bitselector_1_out;
  wire [31:0] ram_1_data;

  BitSelector #(.width(30), .group(7)) bitselector_1 (.in(Read_address[31:2]), .out(bitselector_1_out), .sel(3'b000));
  RAM #(.addrWidth(7), .dataWidth(32), .bus("asynch"), .Datafile_on_reset("TG00rom.txt")) ram_1 (
    .addr(bitselector_1_out), .data(ram_1_data), .sel(1'b1), .ld(1'b1), .clr(1'b0));
  // Delayer2x32 delayer2x32_1: pin names not known; wires that end beside it: ram_1_data, Instruction
endmodule

module InstDecoder (
  input  [31:0] IB,
  output [5:0] IB31_26,
  output [4:0] IB25_21,
  output [4:0] IB20_16,
  output [4:0] IB15_11,
  output [5:0] IB5_0,
  output [15:0] IB15_0,
  output [25:0] IB25_0
);


  assign IB5_0 = IB[5:0];
  assign IB15_0 = IB[15:0];
  assign IB15_11 = IB[15:11];
  assign IB20_16 = IB[20:16];
  assign IB25_0 = IB[25:0];
  assign IB25_21 = IB[25:21];
  assign IB31_26 = IB[31:26];
endmodule

module Control_ALU (
  input  [2:0] OpALU,
  input  [5:0] funcion,
  output [3:0] OUT
);

  wire [3:0] multiplexer_1_out;

  Multiplexer #(.select(4), .width(4), .enable("false")) multiplexer_1 (
    .in0(4'b0010), .in2(4'b0110), .in4(4'b0000), .in5(4'b0001), .in10(4'b0111), .out(multiplexer_1_out),
    .sel(funcion[3:0]));  // open: in1, in3, in6, in7, in8, in9, in11, in12, in13, in14, in15
  Multiplexer #(.select(3), .width(4), .enable("false")) multiplexer_2 (
    .in0(4'b0010), .in1(4'b0110), .in2(4'b0000), .in3(4'b0001), .in4(4'b0111), .in5(4'b1100),
    .in7(multiplexer_1_out), .out(OUT), .sel(OpALU));  // open: in6

  // Notes on the sheet:
  //   OpALU    OUT
  //    000    add
  //    001    sub
  //    010    and
  //    011    or
  //   100    set on less than
  //   101    nor
  //   111    funcion (in)
endmodule

module Unidad_de_Control (
  input  [5:0] OPCODE,
  output HALT,
  output JUMP,
  output RegWrite,
  output MemWrite,
  output MemRead,
  output [2:0] OPALU,
  output RegDST,
  output ALUSrc,
  output ALUtoReg
);

  wire decodificador_uc_1_addi;

  Decodificador_UC decodificador_uc_1 (
    .HALT(HALT), .J(JUMP), .OPCODE(OPCODE), .LW(MemRead), .SW(MemWrite), .ALU(ALUSrc),
    .ADDI(decodificador_uc_1_addi));
  or or_1 (RegWrite, MemRead, decodificador_uc_1_addi, ALUSrc);
  or or_2 (ALUtoReg, ALUSrc, decodificador_uc_1_addi);

  assign OPALU = {3{ALUSrc}};
  assign RegDST = ALUSrc;
endmodule

module Decodificador_UC (
  input  [5:0] OPCODE,
  output HALT,
  output J,
  output SW,
  output LW,
  output ADDI,
  output ALU
);

  and u_HALT (HALT, OPCODE[0], OPCODE[1], OPCODE[2], OPCODE[3], OPCODE[4], OPCODE[5]);
  and u_SW (SW, OPCODE[0], OPCODE[1], ~OPCODE[2], OPCODE[3], ~OPCODE[4], OPCODE[5]);  // AND_Gate
  and u_ADDI (ADDI, ~OPCODE[0], ~OPCODE[1], ~OPCODE[2], OPCODE[3], ~OPCODE[4], ~OPCODE[5]);  // AND_Gate
  and u_J (J, ~OPCODE[0], OPCODE[1], ~OPCODE[2], ~OPCODE[3], ~OPCODE[4], ~OPCODE[5]);  // AND_Gate
  and u_LW (LW, OPCODE[0], OPCODE[1], ~OPCODE[2], ~OPCODE[3], ~OPCODE[4], OPCODE[5]);  // AND_Gate
  and u_ALU (ALU, ~OPCODE[0], ~OPCODE[1], ~OPCODE[2], ~OPCODE[3], ~OPCODE[4], ~OPCODE[5]);  // AND_Gate
endmodule
