// Logisim project suma.circ as structural Verilog
module SUMADOR_RESTADOR (
  input  [7:0] A,
  input  [7:0] B,
  input  SUMA_RESTA,
  output [7:0] SALIDA,
  output CERO,
  output NEGATIVO
);

  wire [7:0] adder_1_out, subtractor_1_out;

  main main_1 ();
  Adder adder_1 (.a(A), .b(B), .out(adder_1_out));  // open: cin, cout
  Subtractor subtractor_1 (.a(A), .b(B), .out(subtractor_1_out));  // open: bin, bout
  // Probe on adder_1_out
  // Probe on subtractor_1_out
  Multiplexer #(.width(8)) multiplexer_1 (
    .in0(adder_1_out), .in1(subtractor_1_out), .out({NEGATIVO, SALIDA[6:0]}), .sel(SUMA_RESTA));  // open: en
  nor nor_1 (CERO, SALIDA[0], SALIDA[1], SALIDA[2], SALIDA[3], SALIDA[4], SALIDA[5], SALIDA[6], NEGATIVO);

  assign SALIDA[7] = NEGATIVO;

  // Other names for the same wires on the sheet: OUT[7:0] = {NEGATIVO, SALIDA[6:0]}
endmodule
